# Fritzing sketch circuit (saved by Fritzing 0.9.3b)
breadboards: 1

parts:
  MH-ET_LIVE_ESP32_DEVKIT1 = MH-ET LIVE ESP32 DEVKIT 38 pins
  RS485_module1 = RS485 Module (MAX3485)
  DMX_PIN2 = Header 1 [package=smtso-256-et]
  DMX_PIN3 = Header 1 [package=smtso-256-et]
  DMX_PIN1 = Header 1 [package=smtso-256-et]

nets:
  5V: MH-ET_LIVE_ESP32_DEVKIT1.5V, RS485_module1.VCC
  GND: MH-ET_LIVE_ESP32_DEVKIT1.GND, RS485_module1.GND, RS485_module1.RE, RS485_module1.DE, DMX_PIN1.1
  N1: MH-ET_LIVE_ESP32_DEVKIT1.RXD0, RS485_module1.RO
  N2: RS485_module1.A, DMX_PIN3.1
  N3: RS485_module1.B, DMX_PIN2.1

custom parts:
  MH-ET LIVE ESP32 DEVKIT 38 pins: http://mh.nodebb.com/topic/2/mh-et-live-esp32-devkit
  RS485 Module (MAX3485): Commercially available RS485 to RS232 TTL Module
